# Fritzing sketch Headset (saved by Fritzing 0.9.2b)
breadboards: 1

parts:
  Part2 = Lilypad Arduino Board
  Part3 = Bluetooth Mate Silver
  U1 = LIPO-2000mAh [package=lipo-2000]
  Part4 = OpenLog
  Part5 = USB LiPoly Charger
  Part1 = LilyPad LiPower

nets:
  GND: Part2.GND, Part3.GND, U1.-, Part4.GND, Part5.GND, Part1.GND
  VCC: Part2.VCC, Part3.VCC, Part4.VCC, Part1.+
  N1: U1.+, Part1.B
  N2: Part5.VBAT, Part1.C
